// Digital circuit Mux21.dig as structural Verilog
module Mux21 (
  input  I0,
  input  I1,
  input  S0
);

  wire and_1_out, and_2_out, not_1_out, or_1_out;

  and and_1 (and_1_out, I0, not_1_out);
  and and_2 (and_2_out, I1, S0);
  not not_1 (not_1_out, S0);
  or or_1 (or_1_out, and_1_out, and_2_out);
  LED led_1 (.in(or_1_out));
endmodule
