// Digital circuit Semisumador.dig as structural Verilog
module Semisumador (
  input  B,
  input  A
);

  wire and_1_out, xor_1_out;

  xor xor_1 (xor_1_out, B, A);
  and and_1 (and_1_out, B, A);
  LED Suma (.in(xor_1_out));
  LED Carry_out (.in(and_1_out));

  // Notes on the sheet:
  //   Primer sumando
  //   Segundo sumando
endmodule
