// Digital circuit SumadorCompleto.dig as structural Verilog
module SumadorCompleto (
  input  A,
  input  B,
  input  Cin
);

  wire and_1_out, and_2_out, or_1_out, or_2_out, xor_1_out, xor_2_out;

  xor xor_1 (xor_1_out, A, B);
  and and_1 (and_1_out, B, A);
  or or_1 (or_1_out, B, A);
  and and_2 (and_2_out, or_1_out, Cin);
  xor xor_2 (xor_2_out, xor_1_out, Cin);
  or or_2 (or_2_out, and_1_out, and_2_out);
  LED S (.in(xor_2_out));
  LED Cout (.in(or_2_out));
endmodule
