// Digital circuit comparador2bits.dig as structural Verilog
module comparador2bits (
  input  A,
  input  B,
  input  C,
  input  D,
  output IGUAL
);

  wire xnor_1_out, xnor_2_out;

  xnor xnor_1 (xnor_1_out, A, C);
  xnor xnor_2 (xnor_2_out, B, D);
  and and_1 (IGUAL, xnor_1_out, xnor_2_out);
endmodule

/* Test case:
A B C D OUT
0 0 0 0 1
0 0 0 1 0
0 0 1 0 0
0 0 1 1 0
0 1 0 0 0
0 1 0 1 1
0 1 1 0 0
0 1 1 1 0
1 0 0 0 0
1 0 0 1 0
1 0 1 0 1
1 0 1 1 0
1 1 0 0 0
1 1 0 1 0
1 1 1 0 0
1 1 1 1 1
*/
