// Digital circuit comparadorbits.dig as structural Verilog
module comparadorbits (
  input  A,
  input  B,
  output IGUAL,
  output MENOR,
  output MAYOR
);

  wire not_1_out, not_2_out;

  not not_1 (not_1_out, A);
  not not_2 (not_2_out, B);
  and and_1 (MENOR, B, not_1_out);
  xnor xnor_1 (IGUAL, A, B);
  and and_2 (MAYOR, A, not_2_out);
endmodule

/* Test case:
A B MENOR IGUAL MAYOR
0 0 0 1 0
0 1 1 0 0 
1 0 0 0 1
1 1 0 1 0
*/
